# Fritzing sketch Fritz JNE Autopilot V6D (saved by Fritzing 0.9.0b)
breadboards: 1

parts:
  C1 = Ceramic Capacitor [capacitance=100nF package="100 mil [THT, multilayer]"]
  C2 = Ceramic Capacitor [capacitance=100nF package="100 mil [THT, multilayer]"]
  C3 = Ceramic Capacitor [capacitance=100nF package="100 mil [THT, multilayer]"]
  C4 = Ceramic Capacitor [capacitance=100nF package="100 mil [THT, multilayer]"]
  C5 = Ceramic Capacitor [capacitance=100nF package="100 mil [THT, multilayer]"]
  IC2 = SP3232E [package="DIP16 [THT]"]
  Part3 = IMU Digital Combo Board 6DOF
  S13 = Toggle Switch [package=THT]
  R4 = Rotary Potentiometer (Small) [maximum_resistance=10kΩ package=THT]
  R8 = Rotary Potentiometer (Small) [maximum_resistance=10kΩ package=THT]
  Arduino2 = Arduino Mega 2560 (Rev3)
  Arduino1 = Arduino Mega 2560 (Rev3)
  R9 = Resistor [tolerance=±5% resistance=4.7 package=THT]
  4x20_LCD_screen_w/Green_Screen1 = 4x20 LCD screen w/Green Screen
  Keypad4x1 = Keypad Membran 4x4
  MD03A1 = Dual VNH2SP30 Motor Driver [part_number=MD03A]
  Part4 = NRF24L01+ Breakout Board
  Part5 = Breadboard Power Supply Board SMD

nets:
  GND: C1.0, C3.0, C4.1, IC2.Out_2, Part3.GND, S13.L1, R4.leg1, R8.leg1, Arduino2.GND, Arduino1.GND, 4x20_LCD_screen_w/Green_Screen1.VSS, 4x20_LCD_screen_w/Green_Screen1.R/W, 4x20_LCD_screen_w/Green_Screen1.LED-, MD03A1.GND, Part4.GND, Part5.GND
  N1: C1.1, IC2.Pin_2_V+
  N2: C2.0, IC2.Pin_3_C1-
  N3: C2.1, IC2.Pin_1_C1+
  N4: C3.1, IC2.Pin_6_V-
  5V: C4.0, IC2.Out_1, Part3.3.3V, S13.L2, R4.leg2, R8.leg2, Arduino2.5V, Arduino1.5V, R9.Pin_0, Part4.VCC, Part5.VCC
  N5: C5.0, IC2.Pin_5_C2-
  N6: C5.1, IC2.Pin_4_C2+
  N7: IC2.Pin_9_R2OUT, Arduino2.D16_PWM/TX2
  N8: IC2.Out_5, Arduino2.D17_PWM/RX2
  N9: Part3.SDA, Arduino1.D20/SDA
  N10: Part3.SCL, Part3.INT1, Arduino1.D21/SCL
  N11: S13.COM, Arduino1.D48
  N12: R4.wiper, Arduino1.A4
  N13: R8.wiper, Arduino1.A2
  N14: Arduino2.D14/TX3, Arduino1.D15/RX3
  N15: Arduino1.D16_PWM/TX2, MD03A1.2PWM
  N16: Arduino1.D10_PWM, Part4.CE
  N17: Arduino1.D9_PWM, Part4.CS
  N18: Arduino1.D2_PWM, Part4.IRQ
  N19: Arduino1.D7_PWM, 4x20_LCD_screen_w/Green_Screen1.V0
  N20: Arduino1.D23, Keypad4x1.Pin7
  N21: Arduino1.D25, Keypad4x1.Pin6
  N22: Arduino1.D27, Keypad4x1.Pin5
  N23: Arduino1.D29, Keypad4x1.Pin4
  N24: Arduino1.D31, Keypad4x1.Pin3
  N25: Arduino1.D33, Keypad4x1.Pin2
  N26: Arduino1.D35, Keypad4x1.Pin1
  N27: Arduino1.D39, 4x20_LCD_screen_w/Green_Screen1.RS
  N28: Arduino1.D41, 4x20_LCD_screen_w/Green_Screen1.E
  N29: Arduino1.D43, 4x20_LCD_screen_w/Green_Screen1.DB4
  N30: Arduino1.D45, 4x20_LCD_screen_w/Green_Screen1.DB5
  N31: Arduino1.D47, 4x20_LCD_screen_w/Green_Screen1.DB6
  N32: Arduino1.D49, 4x20_LCD_screen_w/Green_Screen1.DB7
  N33: Arduino1.D50, Part4.MISO
  N34: Arduino1.D51, Part4.MOSI
  N35: Arduino1.D52, Part4.SCK
  N36: R9.Pin_1, 4x20_LCD_screen_w/Green_Screen1.LED+

notes:
  GPS INPUT
  RS232 in from GPS or PC navigation software.
  Black, Garmin pin5, ground.
  Red, Garmin Tx, Pin 2..
  1 Vss - grnd
  2 Vdd +5V
  3 V0 - pin 7 LCD PWM contrst control or 10K pot
  4 RS - pin 39 (was 41)
  5 RW - grnd
  6 E - pin 41 (was 43)
  7, 8, 9, 10 - none
  11 DB4 - pin 43 (was 45)
  12 DB5 pin 45 (was 47)
  13 DB6 - pin 47 (was 45)
  14 DB7 pin 49 (was 39) used to be on 51 but 51 need for RF remote
  15 LED+ to 5 ohm resistor to +5v,
  16 LED- grnd
  LiquidCrystal lcd(39,41,43,45,47,49);
  (was LiquidCrystal lcd(41,43,45,47,49,39);
  Be sure your code matches your wiring
  COMPASS
  MinIMU-9, 9 DOF gyro Compass (Pololu V3)
  External wiring with telephone RJ-11 6P4C jacks and wire
  KEYPAD
  Use 12 button keypad
  1 2 3
  4 5 6
  7 8 9
  * 0 #
  User must detrmine which keypad pins are columns 1-3 and Rows 1-4. Code declarations must agree with wiring. See Arduino Keypad Tutorial
  Wiring PINS
  Keypad - Arduino Jack's Wiring
  1 - pin 35 32
  2 - pin 33 34
  3 - pin 31 36
  4 - pin 29 38
  5 - pin 27 40
  6 - pin 25 42
  7 - pin 23 44
  See Autopilot code main Tab around line 297
  byte colPins[COLS] = {27,23,31}
  byte rowPins[ROWS] = {25,35,33,29};
  OUTPUT TO RUDDER CONTROL
  Pololu QIK Item 1112
  Your Clutch is wired to Motor 0
  Your Steering motor is wired to Motor 1
  The Mega Serial 2, TX2, pin 16 goes to Qik "TTL serial input RX
  SEE Pololu User's Guide
  STEERING ENABLE SWITCH sw1 (pin 48)
  Must be on to select steering modes and steer. If sw1 already on pressing key 1 sets compass mode and captures current heading as heading_to_steer. If turned off HTS set to 0. Note earlier versions had a sw2 also. SW2 is commented out in the code and could be reinstated if user desired.
  RUDDER POSITION FEEDBACK
  Mounted on rudder shaft. (Analog Pin 4)
  Honeywell Hall Effect rotary Position Sensor 785-RTY090LVNAX .5 V to 4.5 V = -/+45 deg, www.mouser.com
  10 k pot(not required) use for Knob steering.
  Wire +5 V and Grnd. Center pin to Mega pin 42. Wire so turning clockwise increases voltage output.
  POWER SUPPLY
  Use a 5V 3A buck supply with input from ships 12 V battery. Power supply to all 3 boards, use common ground.
  Adjust to 4.85 V. Output to Arduino 5 V bus
  See Autopilot Documentation
  This Mega for GPS processing. Not required for Compass only operation
  Fritz Feb 8, 2016 Broncos won Superbowl yesterday
  This is the basic Fritz wiring diagram for the Jack Edwards Autopilot. It is consistent with Autopilot_JNE_RF24_bno055_J9 as of this date.
  Many of the components shown do not have accurate Fritz parts available. parts manufacturers have data sheets for their integrated parts. They should be consulted when wiring your Autopilot. In this Fritz I show the wiring using a breadboard for many of the connections. An Arduino Mega prototype board is recommended for final wiring because the wiring can be put on the prototype board so that the Arduino Mega can be replaced without rewiring.
  NRF24L01 Radio
  for wireless Remote communication
  NRF24L01 Arduino
  CE pin 9
  CS pin 10
  MISO pin 50 (MISO)
  MOSI pin 51 (MOSI)
  SCK pin 52 (SCK)
  IRQ (interrupt) pin 2
  GENERAL NOTES
  3/8/18 Rev V6D added NRF24l01 radio for wireless remote.
  Verified LCD Pins, added Sparkfun voltage regulator as an example.

custom parts:
  SP3232E: SPIEX ADAPTER, RS232 TO TTL
  4x20 LCD screen w/Green Screen: A standard character display with 4x20 characters.
  Keypad Membran 4x4: Membrane Keypad 4x4 Matrix
